# Fritzing sketch Schematic (saved by Fritzing 0.8.7b)

parts:
  Nano_/_Mega_/_Etc = Arduino Nano (Rev3.0) (ICSP)
  Power_source_under_nano's_limits = Battery Holders [package=battery]
  Geiger_counter = GEIGER_TUBE [package=geiger_tube]
  Any_bluetooth_module_(HC-05_/_HC-06) = Bluetooth HC-06
  (Optional)_SSD1306_Oled_screen = OLED 128x64 I2C Monochrome Display

nets:
  N1: Nano_/_Mega_/_Etc.D1/TX, Any_bluetooth_module_(HC-05_/_HC-06).RXD
  N2: Nano_/_Mega_/_Etc.D0/RX, Any_bluetooth_module_(HC-05_/_HC-06).TXD
  N3: Nano_/_Mega_/_Etc.D3, Geiger_counter.C
  N4: Nano_/_Mega_/_Etc.VIN, Power_source_under_nano's_limits.+
  GND: Nano_/_Mega_/_Etc.GND, Power_source_under_nano's_limits.-, Any_bluetooth_module_(HC-05_/_HC-06).GND, (Optional)_SSD1306_Oled_screen.GND
  5V: Nano_/_Mega_/_Etc.5V, Any_bluetooth_module_(HC-05_/_HC-06).VCC, (Optional)_SSD1306_Oled_screen.VDD
  N5: Nano_/_Mega_/_Etc.A5, (Optional)_SSD1306_Oled_screen.SCK
  N6: Nano_/_Mega_/_Etc.A4, (Optional)_SSD1306_Oled_screen.SDA
